// Logisim project oblig1.circ as structural Verilog: 7 circuits, main circuit main
module main (
  input  [3:0] inn,
  input  in_2,
  output [8:0] out_3
);

  wire [7:0] multiplikator_1_out_2;

  // Probe on inn
  multiplikator multiplikator_1 (.inn(inn), .out_2(multiplikator_1_out_2));
  two_s_compliment two_s_compliment_1 (
    .in_1(multiplikator_1_out_2[7]), .in_2(multiplikator_1_out_2[6]), .in_3(multiplikator_1_out_2[5]),
    .in_4(multiplikator_1_out_2[4]), .in_5(multiplikator_1_out_2[3]), .in_6(multiplikator_1_out_2[2]),
    .in_7(multiplikator_1_out_2[1]), .in_8(multiplikator_1_out_2[0]), .\på_av (in_2), .out_10(out_3[8]),
    .out_11(out_3[7]), .out_12(out_3[6]), .out_13(out_3[5]), .out_14(out_3[4]), .out_15(out_3[3]),
    .out_16(out_3[2]), .out_17(out_3[1]), .out_18(out_3[0]));
  // Probe on out_3
endmodule

// FA
module full_adder (
  input  A,
  input  B,
  input  carry,
  output out,
  output carry_2
);

  wire halv_adder_1_mente, halv_adder_1_out, halv_adder_2_mente;

  halv_adder halv_adder_1 (.A(A), .B(B), .out(halv_adder_1_out), .mente(halv_adder_1_mente));
  halv_adder halv_adder_2 (.A(halv_adder_1_out), .B(carry), .out(out), .mente(halv_adder_2_mente));
  or or_1 (carry_2, halv_adder_1_mente, halv_adder_2_mente);
endmodule

// HA
module halv_adder (
  input  A,
  input  B,
  output out,
  output mente
);

  xor xor_1 (out, A, B);
  and and_1 (mente, A, B);
endmodule

module _4_bit_full_adder (
  input  a2,
  input  b2,
  input  a0,
  input  b0,
  input  a1,
  input  b1,
  input  a3,
  input  b3,
  input  in_9,
  output O1,
  output out2,
  output out4,
  output out3,
  output out0
);

  wire full_adder_1_p3, full_adder_2_p3, full_adder_3_p3;

  // full_adder full_adder_1: pin names not known; wires that end beside it: in_9, a0, full_adder_1_p3, b0, out0
  // full_adder full_adder_2: pin names not known; wires that end beside it: full_adder_1_p3, a1, full_adder_2_p3, b1, O1
  // full_adder full_adder_3: pin names not known; wires that end beside it: full_adder_2_p3, a2, full_adder_3_p3, b2, out2
  // full_adder full_adder_4: pin names not known; wires that end beside it: full_adder_3_p3, a3, out4, b3, out3
endmodule

module _8_bit_adder (
  input  a2,
  input  b2,
  input  a6,
  input  b6,
  input  a0,
  input  b0,
  input  a1,
  input  b1,
  input  a3,
  input  b3,
  input  a4,
  input  b4,
  input  a5,
  input  b5,
  input  a7,
  input  b7,
  input  in_17,
  output O1,
  output out2,
  output out3,
  output out5,
  output out6,
  output out7,
  output out8,
  output out0,
  output out4
);

  wire full_adder_1_p3, full_adder_2_p3, full_adder_3_p3, full_adder_4_p3, full_adder_5_p3, full_adder_6_p3,
       full_adder_7_p3;

  // full_adder full_adder_1: pin names not known; wires that end beside it: in_17, a0, full_adder_1_p3, b0, out0
  // full_adder full_adder_2: pin names not known; wires that end beside it: full_adder_1_p3, a1, full_adder_2_p3, b1, O1
  // full_adder full_adder_3: pin names not known; wires that end beside it: full_adder_2_p3, a2, full_adder_3_p3, b2, out2
  // full_adder full_adder_4: pin names not known; wires that end beside it: full_adder_3_p3, a3, full_adder_4_p3, b3, out3
  // full_adder full_adder_5: pin names not known; wires that end beside it: full_adder_4_p3, a4, full_adder_5_p3, b4, out4
  // full_adder full_adder_6: pin names not known; wires that end beside it: full_adder_5_p3, a5, full_adder_6_p3, b5, out5
  // full_adder full_adder_7: pin names not known; wires that end beside it: full_adder_6_p3, a6, full_adder_7_p3, b6, out6
  // full_adder full_adder_8: pin names not known; wires that end beside it: full_adder_7_p3, a7, out7, b7, out8
endmodule

module two_s_compliment (
  input  in_1,
  input  in_2,
  input  in_3,
  input  in_4,
  input  in_5,
  input  in_6,
  input  in_7,
  input  in_8,
  input  \på_av ,
  output out_10,
  output out_11,
  output out_12,
  output out_13,
  output out_14,
  output out_15,
  output out_16,
  output out_17,
  output out_18
);

  wire halv_adder_1_mente, halv_adder_2_mente, halv_adder_3_mente, halv_adder_4_mente, halv_adder_5_mente,
       halv_adder_6_mente, halv_adder_7_mente, halv_adder_8_mente, xor_1_out, xor_2_out, xor_3_out,
       xor_4_out, xor_5_out, xor_6_out, xor_7_out, xor_8_out;

  xor xor_1 (xor_1_out, in_1, \på_av );
  halv_adder halv_adder_1 (.A(halv_adder_2_mente), .B(xor_1_out), .out(out_11), .mente(halv_adder_1_mente));
  xor xor_2 (xor_2_out, in_2, \på_av );
  halv_adder halv_adder_2 (.A(halv_adder_3_mente), .B(xor_2_out), .out(out_12), .mente(halv_adder_2_mente));
  xor xor_3 (xor_3_out, in_3, \på_av );
  halv_adder halv_adder_3 (.A(halv_adder_4_mente), .B(xor_3_out), .out(out_13), .mente(halv_adder_3_mente));
  xor xor_4 (xor_4_out, in_4, \på_av );
  halv_adder halv_adder_4 (.A(halv_adder_5_mente), .B(xor_4_out), .out(out_14), .mente(halv_adder_4_mente));
  xor xor_5 (xor_5_out, in_5, \på_av );
  halv_adder halv_adder_5 (.A(halv_adder_6_mente), .B(xor_5_out), .out(out_15), .mente(halv_adder_5_mente));
  xor xor_6 (xor_6_out, in_6, \på_av );
  halv_adder halv_adder_6 (.A(halv_adder_7_mente), .B(xor_6_out), .out(out_16), .mente(halv_adder_6_mente));
  xor xor_7 (xor_7_out, in_7, \på_av );
  halv_adder halv_adder_7 (.A(halv_adder_8_mente), .B(xor_7_out), .out(out_17), .mente(halv_adder_7_mente));
  xor xor_8 (xor_8_out, in_8, \på_av );
  halv_adder halv_adder_8 (.A(\på_av ), .B(xor_8_out), .out(out_18), .mente(halv_adder_8_mente));

  assign out_10 = \på_av ;
  // also tied to GND on the sheet: halv_adder_1_mente
endmodule

module multiplikator (
  input  [3:0] inn,
  output [7:0] out_2
);

  wire full_adder_1_carry_2, halv_adder_1_mente, halv_adder_2_mente;

  // Probe on inn
  halv_adder halv_adder_1 (.A(inn[0]), .B(inn[2]), .out(out_2[3]), .mente(halv_adder_1_mente));
  full_adder full_adder_1 (
    .A(inn[1]), .B(inn[3]), .carry(halv_adder_1_mente), .out(out_2[4]), .carry_2(full_adder_1_carry_2));
  halv_adder halv_adder_2 (.A(full_adder_1_carry_2), .B(inn[2]), .out(out_2[5]), .mente(halv_adder_2_mente));
  halv_adder halv_adder_3 (.A(halv_adder_2_mente), .B(inn[3]), .out(out_2[6]), .mente(out_2[7]));
  // Probe on {out_2[7:3], inn[1:0], 1'b0}

  assign out_2[2:0] = {inn[1:0], 1'b0};
endmodule
